// Logisim project 19101284.circ as structural Verilog: 6 circuits, main circuit main
module main (
);

  DotMatrix #(.matrixcols(16), .matrixrows(16)) Monitor_1 ();  // open: col0, col1, col2, col3, col4, col5, col6, col7, col8, col9, col10, col11, col12, col13, col14, col15
  DotMatrix #(.matrixcols(16), .matrixrows(16)) Monitor_2 ();  // open: col0, col1, col2, col3, col4, col5, col6, col7, col8, col9, col10, col11, col12, col13, col14, col15
  DotMatrix #(.matrixcols(16), .matrixrows(16)) Monitor_3 ();  // open: col0, col1, col2, col3, col4, col5, col6, col7, col8, col9, col10, col11, col12, col13, col14, col15
  DotMatrix #(.matrixcols(16), .matrixrows(16)) Monitor_4 ();  // open: col0, col1, col2, col3, col4, col5, col6, col7, col8, col9, col10, col11, col12, col13, col14, col15
endmodule

module HalfAdder (
  input  A,
  input  B,
  output S,
  output C
);

  xor xor_1 (S, A, B);
  and and_1 (C, A, B);
endmodule

module FullAdder (
  input  A,
  input  B,
  input  C_in,
  output S,
  output C_out
);

  wire halfadder_1_c, halfadder_1_s, halfadder_2_c;

  HalfAdder halfadder_1 (.A(A), .B(B), .S(halfadder_1_s), .C(halfadder_1_c));
  HalfAdder halfadder_2 (.A(halfadder_1_s), .B(C_in), .S(S), .C(halfadder_2_c));
  or or_1 (C_out, halfadder_1_c, halfadder_2_c);
endmodule

module MyCounter (
  input  CLK,
  output [7:0] D
);

  wire and_1_out, and_2_out, and_3_out, and_4_out, and_5_out, and_6_out;

  J_K_Flip_Flop j_k_ff_1 (.J(1'b1), .K(1'b1), .clk(CLK), .Q(D[0]));  // open: Qn, preset, reset
  J_K_Flip_Flop j_k_ff_2 (.J(D[0]), .K(D[0]), .clk(CLK), .Q(D[1]));  // open: Qn, preset, reset
  and and_1 (and_1_out, D[0], D[1]);
  J_K_Flip_Flop j_k_ff_3 (.J(and_1_out), .K(and_1_out), .clk(CLK), .Q(D[2]));  // open: Qn, preset, reset
  and and_2 (and_2_out, and_1_out, D[2]);
  J_K_Flip_Flop j_k_ff_4 (.J(and_2_out), .K(and_2_out), .clk(CLK), .Q(D[3]));  // open: Qn, preset, reset
  and and_3 (and_3_out, and_2_out, D[3]);
  J_K_Flip_Flop j_k_ff_5 (.J(and_3_out), .K(and_3_out), .clk(CLK), .Q(D[4]));  // open: Qn, preset, reset
  and and_4 (and_4_out, and_3_out, D[4]);
  J_K_Flip_Flop j_k_ff_6 (.J(and_4_out), .K(and_4_out), .clk(CLK), .Q(D[5]));  // open: Qn, preset, reset
  and and_5 (and_5_out, and_4_out, D[5]);
  J_K_Flip_Flop j_k_ff_7 (.J(and_5_out), .K(and_5_out), .clk(CLK), .Q(D[6]));  // open: Qn, preset, reset
  and and_6 (and_6_out, and_5_out, D[6]);
  J_K_Flip_Flop j_k_ff_8 (.J(and_6_out), .K(and_6_out), .clk(CLK), .Q(D[7]));  // open: Qn, preset, reset
endmodule

module EightBitAdder (
  input  [7:0] A,
  input  [7:0] B,
  output [7:0] S,
  output OVR
);

  wire fulladder_1_c_out, fulladder_2_c_out, fulladder_3_c_out, fulladder_4_c_out, fulladder_5_c_out,
       fulladder_6_c_out, fulladder_7_c_out;

  FullAdder fulladder_1 (.A(A[0]), .B(B[0]), .C_in(1'b0), .S(S[0]), .C_out(fulladder_1_c_out));
  FullAdder fulladder_2 (.A(A[1]), .B(B[1]), .C_in(fulladder_1_c_out), .S(S[1]), .C_out(fulladder_2_c_out));
  FullAdder fulladder_3 (.A(A[2]), .B(B[2]), .C_in(fulladder_2_c_out), .S(S[2]), .C_out(fulladder_3_c_out));
  FullAdder fulladder_4 (.A(A[3]), .B(B[3]), .C_in(fulladder_3_c_out), .S(S[3]), .C_out(fulladder_4_c_out));
  FullAdder fulladder_5 (.A(A[4]), .B(B[4]), .C_in(fulladder_4_c_out), .S(S[4]), .C_out(fulladder_5_c_out));
  FullAdder fulladder_6 (.A(A[5]), .B(B[5]), .C_in(fulladder_5_c_out), .S(S[5]), .C_out(fulladder_6_c_out));
  FullAdder fulladder_7 (.A(A[6]), .B(B[6]), .C_in(fulladder_6_c_out), .S(S[6]), .C_out(fulladder_7_c_out));
  FullAdder fulladder_8 (.A(A[7]), .B(B[7]), .C_in(fulladder_7_c_out), .S(S[7]), .C_out(OVR));
endmodule

module OneOfTwoDecoder (
  input  A,
  input  B,
  output Y0,
  output Y1,
  output Y2,
  output Y3
);

  wire not_1_out, not_2_out;

  not not_1 (not_1_out, A);
  not not_2 (not_2_out, B);
  and and_1 (Y0, not_1_out, not_2_out);
  and and_2 (Y1, A, not_2_out);
  and and_3 (Y2, not_1_out, B);
  and and_4 (Y3, A, B);
endmodule
